# Fritzing sketch Mqtt_ESP_Nano_V2 (saved by Fritzing 0.9.3b)
circuit board: 8.46667cm x 5.64444cm
breadboards: 1

parts:
  Componente1 = Arduino Nano (Rev3.0)
  S1 = Round Pushbutton
  S2 = Round Pushbutton
  S3 = Round Pushbutton
  S4 = Round Pushbutton
  J1 = Piezo Speaker

nets:
  N1: Componente1.GND, S1.leg1, S2.leg0, S3.leg1, S4.leg0, J1.pin1
  N2: Componente1.D2, S4.leg1
  N3: Componente1.D3, S3.leg0
  N4: Componente1.D4, S2.leg1
  N5: Componente1.D5, S1.leg0
  N6: Componente1.D6, J1.pin2
